// Logisim project andreialvesfracalossi_CPU_RISC.circ as structural Verilog
// A
module main (
);

  wire clock_1_out, d_ff_1_q, d_ff_2_q, not_1_out, not_2_out, Reset_out, uc_1_clk_ac, uc_1_clk_pc,
       uc_1_clk_ram, uc_1_clk_ri, uc_1_d, uc_1_e, uc_1_load, uc_1_r_w, uc_1_rst_pc, ula_1_ovf, ula_1_zero;
  wire [2:0] \uc_1_operação ;
  wire [3:0] ac_1_out_3, mux_1_s, P_q, ram_1_data, uc_1_b_end, uc_1_dados, uc_1_operando, ula_1_s;
  wire [7:0] ir_1_q, rom_1_data;

  not not_1 (not_1_out, uc_1_load);
  Counter #(.width(4), .max('hf), .trigger("falling")) P (
    .load(uc_1_load), .D(uc_1_dados), .count(not_1_out), .Q(P_q), .clk(uc_1_clk_pc), .clr(uc_1_rst_pc));  // open: carry
  UC uc_1 (
    .B_End(uc_1_b_end), .Operando(uc_1_operando), .D(uc_1_d), .E(uc_1_e), .\Instrução (ir_1_q),
    .\Operação (\uc_1_operação ), .Clock(clock_1_out), .Reset(Reset_out), .Rst_PC(uc_1_rst_pc),
    .Clk_RI(uc_1_clk_ri), .Clk_PC(uc_1_clk_pc), .Clk_AC(uc_1_clk_ac), .Clk_RAM(uc_1_clk_ram),
    .Zero(d_ff_2_q), .Ovf(d_ff_1_q), .Load(uc_1_load), .Dados(uc_1_dados), .R_W(uc_1_r_w));
  Clock clock_1 (.out(clock_1_out));
  IR ir_1 (.D(rom_1_data), .Clock(uc_1_clk_ri), .Q(ir_1_q));
  Button Reset (.out(Reset_out));
  ROM #(.addrWidth(4)) rom_1 (.addr(P_q), .data(rom_1_data));  // open: sel
  // Probe on ac_1_out_3
  ULA ula_1 (
    .D(uc_1_d), .A(ac_1_out_3), .B(mux_1_s), .\Operações (\uc_1_operação ), .S(ula_1_s), .OVF(ula_1_ovf),
    .Zero(ula_1_zero));
  AC ac_1 (.in_2(ula_1_s), .out_3(ac_1_out_3), .Clock(uc_1_clk_ac));
  MUX mux_1 (.A(uc_1_operando), .C(uc_1_e), .B(ram_1_data), .S(mux_1_s));
  // Probe on mux_1_s
  // Probe on ula_1_s
  RAM #(.addrWidth(4), .dataWidth(4)) ram_1 (
    .addr(uc_1_b_end), .data(ram_1_data), .clk(uc_1_clk_ram), .ld(uc_1_r_w));  // open: sel, clr
  D_Flip_Flop d_ff_1 (.clk(uc_1_clk_ac), .D(ula_1_ovf), .Q(d_ff_1_q));  // open: Qn, preset, en, reset
  D_Flip_Flop d_ff_2 (.clk(uc_1_clk_ac), .D(ula_1_zero), .Q(d_ff_2_q));  // open: Qn, preset, en, reset
  BUF_4 buf_4_1 (.in_1(ac_1_out_3), .in_2(not_2_out), .out_3(ram_1_data));
  not not_2 (not_2_out, uc_1_r_w);

  // Notes on the sheet:
  //   000
  //   MOV
  //   0
  //   1
  //   000
  //   MOV
  //   ADD
  //   2
  //   001
  //   3
  //   001
  //   ADD
  //   010
  //   SUB
  //   4
  //   010
  //   5
  //   SUB
  //   011
  //   OR
  //   6
  //   OR
  //   7
  //   011
  //   NOT
  //   8
  //   100
  //   100
  //   NOT
  //   9
  //   101
  //   A
  //   SHF
  //   101
  //   B
  //   SHF
  //   JPZ
  //   C
  //   110
  //   110
  //   JPO
  //   D
  //   111
  //   GO
  //   E
  //   STR
  //   111
  //   F
  //   Instruction Set
  //   0
  //   AC <= X
  //   1
  //   AC <= M(X)
  //   0
  //   AC <= AC+X
  //   1
  //   AC <= AC+M(X)
  //   0
  //   AC <= AC-X
  //   1
  //   AC <= AC-M(X)
  //   0
  //   AC <= AC OR X
  //   1
  //   AC <= AC OR M(X)
  //   0
  //   AC <= NOT X
  //   1
  //   AC <= NOT M( X)
  //   0
  //   AC <= AC << Q
  //   1
  //   AC <= AC >> Q
  //   0
  //   1
  //   PC <= X
  //   0
  //   M(X) <= AC 
  //   1
  //   PC <= X SE FLAG Z
  //   PC <= X SE FLAG O
  //   contents of rom_1 (hex, n*v repeats v):
  //   0 f0 1 f1 10 31 d0 f2 11 f0 12 f1 e4
endmodule

module ADD_1 (
  input  A,
  input  B,
  input  Vem_1,
  output S,
  output Vai_1
);

  wire and_1_out, and_2_out, or_1_out, xor_1_out;

  xor xor_1 (xor_1_out, A, B);
  or or_1 (or_1_out, B, Vem_1);
  and and_1 (and_1_out, or_1_out, A);
  and and_2 (and_2_out, B, Vem_1);
  xor xor_2 (S, xor_1_out, Vem_1);
  or or_2 (Vai_1, and_1_out, and_2_out);
endmodule

module ADD_4 (
  input  [3:0] A,
  input  [3:0] B,
  input  in_3,
  output out_4,
  output [3:0] out_5
);

  wire add_1_1_vai_1, add_1_3_vai_1, add_1_4_vai_1;

  ADD_1 add_1_1 (.A(A[2]), .B(B[2]), .Vem_1(add_1_3_vai_1), .S(out_5[2]), .Vai_1(add_1_1_vai_1));
  ADD_1 add_1_2 (.A(A[3]), .B(B[3]), .Vem_1(add_1_1_vai_1), .S(out_5[3]), .Vai_1(out_4));
  ADD_1 add_1_3 (.A(A[1]), .B(B[1]), .Vem_1(add_1_4_vai_1), .S(out_5[1]), .Vai_1(add_1_3_vai_1));
  ADD_1 add_1_4 (.A(A[0]), .B(B[0]), .Vem_1(in_3), .S(out_5[0]), .Vai_1(add_1_4_vai_1));
endmodule

module SUB_1 (
  input  A,
  input  B,
  input  Vem_1,
  output S,
  output Vai_1
);

  wire and_1_out, and_2_out, or_1_out, xor_1_out;

  xor xor_1 (xor_1_out, A, B);
  or or_1 (or_1_out, B, Vem_1);
  and and_1 (and_1_out, or_1_out, ~A);  // AND_Gate
  and and_2 (and_2_out, B, Vem_1);
  xor xor_2 (S, xor_1_out, Vem_1);
  or or_2 (Vai_1, and_1_out, and_2_out);
endmodule

module SUB_4 (
  input  [3:0] B,
  input  [3:0] A,
  input  Vem_1,
  output Overflow,
  output [3:0] out_5
);

  wire sub_1_2_vai_1, sub_1_3_vai_1, sub_1_4_vai_1;

  SUB_1 sub_1_1 (.A(A[3]), .B(B[3]), .Vem_1(sub_1_2_vai_1), .S(out_5[3]), .Vai_1(Overflow));
  SUB_1 sub_1_2 (.A(A[2]), .B(B[2]), .Vem_1(sub_1_3_vai_1), .S(out_5[2]), .Vai_1(sub_1_2_vai_1));
  SUB_1 sub_1_3 (.A(A[1]), .B(B[1]), .Vem_1(sub_1_4_vai_1), .S(out_5[1]), .Vai_1(sub_1_3_vai_1));
  SUB_1 sub_1_4 (.A(A[0]), .B(B[0]), .Vem_1(Vem_1), .S(out_5[0]), .Vai_1(sub_1_4_vai_1));
endmodule

module DEC3x8 (
  input  [2:0] in_1,
  output S0,
  output S1,
  output S2,
  output S3,
  output S4,
  output S5,
  output S6,
  output S7
);

  wire not_1_out, not_2_out, not_3_out, not_4_out, not_5_out, not_6_out, not_7_out, not_8_out, not_9_out,
       not_10_out, not_11_out, not_12_out;

  not not_1 (not_1_out, in_1[2]);
  not not_2 (not_2_out, in_1[1]);
  not not_3 (not_3_out, in_1[0]);
  not not_4 (not_4_out, in_1[2]);
  not not_5 (not_5_out, in_1[1]);
  not not_6 (not_6_out, in_1[2]);
  not not_7 (not_7_out, in_1[0]);
  not not_8 (not_8_out, in_1[2]);
  not not_9 (not_9_out, in_1[1]);
  not not_10 (not_10_out, in_1[0]);
  not not_11 (not_11_out, in_1[1]);
  not not_12 (not_12_out, in_1[0]);
  and and_1 (S7, in_1[2], in_1[1], in_1[0]);
  and and_2 (S0, not_1_out, not_2_out, not_3_out);
  and and_3 (S1, not_4_out, not_5_out, in_1[0]);
  and and_4 (S2, not_6_out, in_1[1], not_7_out);
  and and_5 (S3, not_8_out, in_1[1], in_1[0]);
  and and_6 (S4, in_1[2], not_9_out, not_10_out);
  and and_7 (S5, in_1[2], not_11_out, in_1[0]);
  and and_8 (S6, in_1[2], in_1[1], not_12_out);
endmodule

module BUF_4 (
  input  [3:0] in_1,
  input  in_2,
  output [3:0] out_3
);

  assign out_3[3] = in_2 ? in_1[3] : 1'bz;  // Controlled_Buffer controlled_buffer_1
  assign out_3[2] = in_2 ? in_1[2] : 1'bz;  // Controlled_Buffer controlled_buffer_2
  assign out_3[1] = in_2 ? in_1[1] : 1'bz;  // Controlled_Buffer controlled_buffer_3
  assign out_3[0] = in_2 ? in_1[0] : 1'bz;  // Controlled_Buffer controlled_buffer_4
endmodule

module BUF_INV_4 (
  input  [3:0] in_1,
  input  in_2,
  output [3:0] out_3
);

  assign out_3[3] = in_2 ? ~in_1[3] : 1'bz;  // Controlled_Inverter controlled_inverter_1
  assign out_3[1] = in_2 ? ~in_1[1] : 1'bz;  // Controlled_Inverter controlled_inverter_2
  assign out_3[2] = in_2 ? ~in_1[2] : 1'bz;  // Controlled_Inverter controlled_inverter_3
  assign out_3[0] = in_2 ? ~in_1[0] : 1'bz;  // Controlled_Inverter controlled_inverter_4
endmodule

module ROT_L (
  input  [3:0] ABCD,
  input  [1:0] xy,
  output [3:0] abcd_2
);

  wire and_1_out, and_2_out, and_3_out, and_4_out, and_5_out, and_6_out, and_7_out, and_8_out, and_9_out;

  and and_1 (and_1_out, ~xy[0], ~xy[1], ABCD[3]);  // AND_Gate
  and and_2 (and_2_out, ~xy[1], xy[0], ABCD[2]);  // AND_Gate
  and and_3 (and_3_out, xy[1], ~xy[0], ABCD[1]);  // AND_Gate
  and and_4 (and_4_out, xy[1], xy[0], ABCD[0]);
  and and_5 (and_5_out, ~xy[1], ~xy[0], ABCD[2]);  // AND_Gate
  and and_6 (and_6_out, ~xy[1], xy[0], ABCD[1]);  // AND_Gate
  and and_7 (and_7_out, xy[1], ~xy[0], ABCD[0]);  // AND_Gate
  and and_8 (and_8_out, ~xy[1], ~xy[0], ABCD[1]);  // AND_Gate
  and and_9 (and_9_out, ~xy[1], xy[0], ABCD[0]);  // AND_Gate
  and and_10 (abcd_2[0], ~xy[1], ~xy[0], ABCD[0]);  // AND_Gate
  or or_1 (abcd_2[3], and_1_out, and_2_out, and_3_out, and_4_out);
  or or_2 (abcd_2[2], and_5_out, and_6_out, and_7_out);
  or or_3 (abcd_2[1], and_8_out, and_9_out);
endmodule

module ROT_R (
  input  [3:0] ABCD,
  input  [1:0] xy,
  output [3:0] abcd_2
);

  wire and_1_out, and_2_out, and_3_out, and_4_out, and_5_out, and_6_out, and_7_out, and_8_out, and_9_out;

  and and_1 (and_1_out, ~xy[0], ~xy[1], ABCD[0]);  // AND_Gate
  and and_2 (and_2_out, ~xy[1], xy[0], ABCD[1]);  // AND_Gate
  and and_3 (and_3_out, xy[1], ~xy[0], ABCD[2]);  // AND_Gate
  and and_4 (and_4_out, xy[1], xy[0], ABCD[3]);
  and and_5 (and_5_out, ~xy[1], ~xy[0], ABCD[1]);  // AND_Gate
  and and_6 (and_6_out, ~xy[1], xy[0], ABCD[2]);  // AND_Gate
  and and_7 (and_7_out, xy[1], ~xy[0], ABCD[3]);  // AND_Gate
  and and_8 (and_8_out, ~xy[1], ~xy[0], ABCD[2]);  // AND_Gate
  and and_9 (and_9_out, ~xy[1], xy[0], ABCD[3]);  // AND_Gate
  and and_10 (abcd_2[3], ~xy[1], ~xy[0], ABCD[3]);  // AND_Gate
  or or_1 (abcd_2[0], and_1_out, and_2_out, and_3_out, and_4_out);
  or or_2 (abcd_2[1], and_5_out, and_6_out, and_7_out);
  or or_3 (abcd_2[2], and_8_out, and_9_out);
endmodule

module OR_4 (
  input  [3:0] A,
  input  [3:0] B,
  output [3:0] out_3
);

  or or_1 (out_3[1], A[1], B[1]);
  or or_2 (out_3[0], A[0], B[0]);
  or or_3 (out_3[2], A[2], B[2]);
  or or_4 (out_3[3], A[3], B[3]);
endmodule

module ULA (
  input  D,
  input  [3:0] A,
  input  [3:0] B,
  input  [2:0] \Operações ,
  output OVF,
  output [3:0] S,
  output Zero
);

  wire add_4_1_out_4, and_1_out, and_2_out, dec3x8_1_s0, dec3x8_1_s1, dec3x8_1_s2, dec3x8_1_s3, dec3x8_1_s4,
       dec3x8_1_s5, dec3x8_1_s6, dec3x8_1_s7, not_2_out, or_2_out, sub_4_1_overflow;
  wire [3:0] add_4_1_out_5, buf_4_6_out_3, or_4_1_out_3, rot_l_1_abcd_2, rot_r_1_abcd_2, sub_4_1_out_5;

  or or_1 (OVF, and_1_out, and_2_out);
  and and_1 (and_1_out, add_4_1_out_4, dec3x8_1_s1);
  and and_2 (and_2_out, sub_4_1_overflow, dec3x8_1_s2);
  BUF_4 buf_4_1 (.in_1(B), .in_2(dec3x8_1_s0), .out_3(S));
  DEC3x8 dec3x8_1 (
    .S0(dec3x8_1_s0), .S1(dec3x8_1_s1), .S2(dec3x8_1_s2), .S3(dec3x8_1_s3), .S4(dec3x8_1_s4),
    .S5(dec3x8_1_s5), .S6(dec3x8_1_s6), .S7(dec3x8_1_s7), .in_1(\Operações ));
  or or_2 (or_2_out, dec3x8_1_s7, dec3x8_1_s6, S[0], S[1], S[2], S[3]);
  ADD_4 add_4_1 (.A(A), .B(B), .in_3(1'b0), .out_5(add_4_1_out_5), .out_4(add_4_1_out_4));
  BUF_4 buf_4_2 (.in_1(add_4_1_out_5), .in_2(dec3x8_1_s1), .out_3(S));
  not not_1 (Zero, or_2_out);
  SUB_4 sub_4_1 (.A(A), .Overflow(sub_4_1_overflow), .B(B), .Vem_1(1'b0), .out_5(sub_4_1_out_5));
  BUF_4 buf_4_3 (.in_1(sub_4_1_out_5), .in_2(dec3x8_1_s2), .out_3(S));
  OR_4 or_4_1 (.A(A), .B(B), .out_3(or_4_1_out_3));
  BUF_4 buf_4_4 (.in_1(or_4_1_out_3), .in_2(dec3x8_1_s3), .out_3(S));
  not not_2 (not_2_out, D);
  BUF_INV_4 buf_inv_4_1 (.in_1(B), .in_2(dec3x8_1_s4), .out_3(S));
  ROT_R rot_r_1 (.abcd_2(rot_r_1_abcd_2), .ABCD(A), .xy(B[1:0]));
  ROT_L rot_l_1 (.abcd_2(rot_l_1_abcd_2), .ABCD(A), .xy(B[1:0]));
  BUF_4 buf_4_5 (.in_1(buf_4_6_out_3), .in_2(dec3x8_1_s5), .out_3(S));
  BUF_4 buf_4_6 (.in_1(rot_r_1_abcd_2), .in_2(D), .out_3(buf_4_6_out_3));
  BUF_4 buf_4_7 (.in_1(rot_l_1_abcd_2), .in_2(not_2_out), .out_3(buf_4_6_out_3));
endmodule

module AC (
  input  Clock,
  input  [3:0] in_2,
  output [3:0] out_3
);

  D_Flip_Flop d_ff_1 (.clk(Clock), .D(in_2[1]), .Q(out_3[1]));  // open: Qn, preset, en, reset
  D_Flip_Flop d_ff_2 (.clk(Clock), .D(in_2[0]), .Q(out_3[0]));  // open: Qn, preset, en, reset
  D_Flip_Flop d_ff_3 (.clk(Clock), .D(in_2[2]), .Q(out_3[2]));  // open: Qn, preset, en, reset
  D_Flip_Flop d_ff_4 (.clk(Clock), .D(in_2[3]), .Q(out_3[3]));  // open: Qn, preset, en, reset
endmodule

module MUX (
  input  [3:0] A,
  input  [3:0] B,
  input  C,
  output [3:0] S
);

  wire not_1_out;

  not not_1 (not_1_out, C);
  BUF_4 buf_4_1 (.in_1(A), .in_2(not_1_out), .out_3(S));
  BUF_4 buf_4_2 (.in_1(B), .in_2(C), .out_3(S));
endmodule

module IR (
  input  Clock,
  input  [7:0] D,
  output [7:0] Q
);

  D_Flip_Flop d_ff_1 (.clk(Clock), .D(D[7]), .Q(Q[7]));  // open: Qn, preset, en, reset
  D_Flip_Flop d_ff_2 (.clk(Clock), .D(D[5]), .Q(Q[5]));  // open: Qn, preset, en, reset
  D_Flip_Flop d_ff_3 (.clk(Clock), .D(D[6]), .Q(Q[6]));  // open: Qn, preset, en, reset
  D_Flip_Flop d_ff_4 (.clk(Clock), .D(D[4]), .Q(Q[4]));  // open: Qn, preset, en, reset
  D_Flip_Flop d_ff_5 (.clk(Clock), .D(D[3]), .Q(Q[3]));  // open: Qn, preset, en, reset
  D_Flip_Flop d_ff_6 (.clk(Clock), .D(D[2]), .Q(Q[2]));  // open: Qn, preset, en, reset
  D_Flip_Flop d_ff_7 (.clk(Clock), .D(D[1]), .Q(Q[1]));  // open: Qn, preset, en, reset
  D_Flip_Flop d_ff_8 (.clk(Clock), .D(D[0]), .Q(Q[0]));  // open: Qn, preset, en, reset
endmodule

module UC (
  input  Clock,
  input  Reset,
  input  [7:0] \Instrução ,
  input  Zero,
  input  Ovf,
  output Clk_RI,
  output Clk_PC,
  output Clk_AC,
  output Rst_PC,
  output Clk_RAM,
  output [3:0] Dados,
  output [3:0] B_End,
  output [3:0] Operando,
  output D,
  output E,
  output [2:0] \Operação ,
  output R_W,
  output Load
);

  wire GoTo_out, JPO_out, JPZ_out, nand_2_out;
  wire [1:0] counter_1_q;

  and GoTo (GoTo_out, \Instrução [7], \Instrução [6], \Instrução [5], ~\Instrução [4], Clk_PC);  // AND_Gate
  nand nand_1 (R_W, Clk_AC, \Instrução [7], \Instrução [6], \Instrução [5], \Instrução [4]);
  Counter #(.width(2), .max('h3)) counter_1 (.Q(counter_1_q), .clk(Clock), .clr(Reset));  // open: load, D, count, carry
  and JPO (JPO_out, \Instrução [7], \Instrução [6], ~\Instrução [5], \Instrução [4], Clk_PC, Ovf);  // AND_Gate
  or or_1 (Load, GoTo_out, JPO_out, JPZ_out);
  and JPZ (JPZ_out, \Instrução [7], \Instrução [6], ~\Instrução [5], ~\Instrução [4], Clk_PC, Zero);  // AND_Gate
  and and_1 (Clk_RI, ~counter_1_q[0], ~counter_1_q[1]);  // AND_Gate
  and and_2 (Clk_PC, counter_1_q[0], ~counter_1_q[1]);  // AND_Gate
  and and_3 (Clk_AC, ~counter_1_q[0], counter_1_q[1]);  // AND_Gate
  and and_4 (Clk_RAM, counter_1_q[0], counter_1_q[1]);
  and and_5 (E, \Instrução [4], nand_2_out);
  nand nand_2 (nand_2_out, \Instrução [7], ~\Instrução [6], \Instrução [5]);  // NAND_Gate

  assign B_End = \Instrução [3:0];
  assign D = \Instrução [4];
  assign Dados = \Instrução [3:0];
  assign Operando = \Instrução [3:0];
  assign \Operação  = \Instrução [7:5];
  assign Rst_PC = Reset;
endmodule
